# Fritzing sketch carrito que para (saved by Fritzing 0.9.3b)
breadboards: 1

parts:
  BUZZER1 = Piezo Speaker
  2N2222 = NPN-Transistor [package="TO92 [THT]"]
  Componente1 = Arduino Uno (Rev3) - ICSP
  VCC1 = Battery block 9V
  INTERRUPTOR = Round Pushbutton
  MOTOR1 = DC Motor
  MOTOR2 = DC Motor
  HC-SR04_Sensor_2 = HC-SR04 Ultrasonic Distance Sensor

nets:
  N1: BUZZER1.pin1, Componente1.ICSP_MOSI, Componente1.D11_PWM/MOSI
  N2: BUZZER1.pin2, Componente1.D10_PWM/SS
  N3: 2N2222.E, MOTOR1.pin_2, MOTOR2.pin_2
  N4: 2N2222.B, Componente1.D12/MISO
  5V: 2N2222.C, Componente1.5V, VCC1.+, HC-SR04_Sensor_2.VCC
  N5: Componente1.D2, HC-SR04_Sensor_2.ECHO
  N6: Componente1.D3_PWM, HC-SR04_Sensor_2.TRIG
  GND: Componente1.GND, INTERRUPTOR.leg1, MOTOR1.pin_1, MOTOR2.pin_1, HC-SR04_Sensor_2.GND
  N7: VCC1.-, INTERRUPTOR.leg0

custom parts:
  HC-SR04 Ultrasonic Distance Sensor: The HC-SR04 is an ultrasonic distance sensor. It is capable of providing measurement for ranges of 2cm to 400cm. The module operates at 5V.
